# Fritzing sketch savebutton-hardware-cjmcu_beetle (saved by Fritzing 0.9.3b)
breadboards: 1

parts:
  JP1 = Header 1 [package=smtso-256-et]  # not connected
  JP2 = Header 1 [package=smtso-256-et]  # not connected
  JP3 = Header 1 [package=smtso-256-et]  # not connected
  JP4 = Header 1 [package=smtso-256-et]  # not connected
  JP5 = Header 1 [package=smtso-256-et]
  JP6 = Header 1 [package=smtso-256-et]
  JP7 = Header 1 [package=smtso-256-et]
  JP8 = Header 1 [package=smtso-256-et]  # not connected
  JP9 = Header 1 [package=smtso-256-et]  # not connected
  JP10 = Header 1 [package=smtso-256-et]  # not connected
  JP11 = Header 1 [package=smtso-256-et]
  JP12 = Header 1 [package=smtso-256-et]  # not connected
  JP13 = Header 1 [package=smtso-256-et]
  JP14 = Header 1 [package=smtso-256-et]  # not connected
  JP15 = Header 1 [package=smtso-256-et]  # not connected
  JP16 = Header 1 [package=smtso-256-et]  # not connected
  LED1 = LEDs [package=led10mm]
  S1 = Round Pushbutton
  R1 = Resistor [tolerance=±5% resistance=330 package="2512 [SMD]"]
  R2 = Resistor [tolerance=±5% resistance=220 package=THT]
  R3 = Resistor [tolerance=±5% resistance=220 package=THT]

nets:
  N1: JP5.1, S1.leg0, R2.Pin_0
  N2: JP6.1, JP13.1, LED1.A, S1.leg1, R3.Pin_0
  N3: JP7.1, R1.Pin_1
  N4: JP11.1, R2.Pin_1, R3.Pin_1
  N5: LED1.C, R1.Pin_0

notes:
  GND
  5V
  D11
  D10
  D9
  CJMCU-Beetle
  ATMega32U4
  330‎ Ω
  button
  OS
  LED
  10‎ kΩ
  OS switch (close: Mac, open: Linux/Windows)
